// Logisim project CTRL.circ as structural Verilog: 4 circuits, main circuit main
module main (
  input  rclr,
  input  [7:0] ir
);

  wire clock_1_out, controlled_buffer_1_out, decoder_hlt;

  Clock clock_1 (.out(clock_1_out));
  Hex_Digit_Display #(.decimalPoint("false")) irrr (.value(ir[7:4]));
  assign controlled_buffer_1_out = decoder_hlt ? clock_1_out : 1'bz;  // Controlled_Buffer controlled_buffer_1
  Hex_Digit_Display #(.decimalPoint("false")) irr (.value(ir[3:0]));
  Tring ring (.CLK(controlled_buffer_1_out), .CLR(rclr));  // open: T
  DEC decoder (
    .IR(ir), .HLT(decoder_hlt));  // open: NOP, CLX, CLY, CLA, OUX, OUY, OUA, CMX, CMY, CMA, CMI, CALL, RET, JZ, JL, JG, JE, ADX, ADY, ADA, ADI, SUX, SUY, SUA, SUI, LDX, LDXI, LDY, LDYI, LDA, LDAI, MXY, MXA, MYX, MYA, MAX, MAY, ANX, ANY, ANA, ANI, ORX, ORY, ORA, ORI, XOX, XOY, XOA, XOI, NOX, NOY, NOA, NOI, STX, STY, STA, LSX, LSY, LSA
endmodule

module DEC (
  input  [7:0] IR,
  output NOP,
  output CLX,
  output CLY,
  output CLA,
  output OUX,
  output OUY,
  output OUA,
  output CMX,
  output CMY,
  output CMA,
  output CMI,
  output CALL,
  output RET,
  output HLT,
  output JZ,
  output JL,
  output JG,
  output JE,
  output ADX,
  output ADY,
  output ADA,
  output ADI,
  output SUX,
  output SUY,
  output SUA,
  output SUI,
  output LDX,
  output LDXI,
  output LDY,
  output LDYI,
  output LDA,
  output LDAI,
  output MXY,
  output MXA,
  output MYX,
  output MYA,
  output MAX,
  output MAY,
  output ANX,
  output ANY,
  output ANA,
  output ANI,
  output ORX,
  output ORY,
  output ORA,
  output ORI,
  output XOX,
  output XOY,
  output XOA,
  output XOI,
  output NOX,
  output NOY,
  output NOA,
  output NOI,
  output STX,
  output STY,
  output STA,
  output LSX,
  output LSY,
  output LSA
);

  wire [7:0] not_1_out;

  assign not_1_out = ~IR;  // NOT_Gate not_1, 8 bits wide
  nand nand_1 (NOP, not_1_out[0], not_1_out[1], not_1_out[2], not_1_out[3], not_1_out[4], not_1_out[5], not_1_out[6], not_1_out[7]);
  nand nand_2 (CLX, IR[0], not_1_out[1], not_1_out[2], not_1_out[3], not_1_out[4], not_1_out[5], not_1_out[6], not_1_out[7]);
  nand nand_3 (CLY, not_1_out[0], IR[1], not_1_out[2], not_1_out[3], not_1_out[4], not_1_out[5], not_1_out[6], not_1_out[7]);
  nand nand_4 (CLA, IR[0], IR[1], not_1_out[2], not_1_out[3], not_1_out[4], not_1_out[5], not_1_out[6], not_1_out[7]);
  nand nand_5 (OUX, not_1_out[0], not_1_out[1], IR[2], not_1_out[3], not_1_out[4], not_1_out[5], not_1_out[6], not_1_out[7]);
  nand nand_6 (OUY, IR[0], not_1_out[1], IR[2], not_1_out[3], not_1_out[4], not_1_out[5], not_1_out[6], not_1_out[7]);
  nand nand_7 (OUA, not_1_out[0], IR[1], IR[2], not_1_out[3], not_1_out[4], not_1_out[5], not_1_out[6], not_1_out[7]);
  nand nand_8 (CMX, IR[0], IR[1], IR[2], not_1_out[3], not_1_out[4], not_1_out[5], not_1_out[6], not_1_out[7]);
  nand nand_9 (CMY, not_1_out[0], not_1_out[1], not_1_out[2], IR[3], not_1_out[4], not_1_out[5], not_1_out[6], not_1_out[7]);
  nand nand_10 (CMA, IR[0], not_1_out[0], not_1_out[1], IR[3], not_1_out[4], not_1_out[5], not_1_out[6], not_1_out[7]);
  nand nand_11 (CMI, not_1_out[0], IR[1], not_1_out[2], IR[3], not_1_out[4], not_1_out[5], not_1_out[6], not_1_out[7]);
  nand nand_12 (CALL, IR[0], IR[1], not_1_out[2], IR[3], not_1_out[4], not_1_out[5], not_1_out[6], not_1_out[7]);
  nand nand_13 (RET, not_1_out[0], not_1_out[1], IR[2], IR[3], not_1_out[4], not_1_out[5], not_1_out[6], not_1_out[7]);
  nand nand_14 (HLT, IR[0], IR[1], IR[2], IR[3], IR[4], IR[5], IR[6], IR[7]);
  nand nand_15 (JZ, not_1_out[0], not_1_out[1], not_1_out[2], not_1_out[3], IR[4], not_1_out[5], not_1_out[6], not_1_out[7]);
  nand nand_16 (JL, not_1_out[0], not_1_out[1], not_1_out[2], not_1_out[3], IR[4], not_1_out[5], not_1_out[6], not_1_out[7]);
  nand nand_17 (JG, not_1_out[0], IR[1], not_1_out[2], not_1_out[3], IR[4], not_1_out[5], not_1_out[6], not_1_out[7]);
  nand nand_18 (JE, IR[0], IR[1], not_1_out[2], not_1_out[3], IR[4], not_1_out[5], not_1_out[6], not_1_out[7]);
  nand nand_19 (ADX, not_1_out[0], not_1_out[1], IR[2], not_1_out[3], IR[4], not_1_out[5], not_1_out[6], not_1_out[7]);
  nand nand_20 (ADY, IR[0], not_1_out[1], IR[2], not_1_out[3], IR[4], not_1_out[5], not_1_out[6], not_1_out[7]);
  nand nand_21 (ADA, not_1_out[0], IR[1], IR[2], not_1_out[3], IR[4], not_1_out[5], not_1_out[6], not_1_out[7]);
  nand nand_22 (ADI, IR[0], IR[1], IR[2], not_1_out[3], IR[4], not_1_out[5], not_1_out[6], not_1_out[7]);
  nand nand_23 (SUX, not_1_out[0], not_1_out[1], not_1_out[2], IR[3], IR[4], not_1_out[5], not_1_out[6], not_1_out[7]);
  nand nand_24 (SUY, IR[0], not_1_out[1], not_1_out[2], IR[3], IR[4], not_1_out[5], not_1_out[6], not_1_out[7]);
  nand nand_25 (SUA, not_1_out[0], IR[1], not_1_out[2], IR[3], IR[4], not_1_out[5], not_1_out[6], not_1_out[7]);
  nand nand_26 (SUI, IR[0], IR[1], not_1_out[2], IR[3], IR[4], not_1_out[5], not_1_out[6], not_1_out[7]);
  nand nand_27 (LDX, not_1_out[0], not_1_out[1], not_1_out[2], not_1_out[3], not_1_out[4], IR[4], not_1_out[6], not_1_out[7]);
  nand nand_28 (LDXI, IR[0], not_1_out[1], not_1_out[2], not_1_out[3], not_1_out[4], IR[5], not_1_out[6], not_1_out[7]);
  nand nand_29 (LDY, not_1_out[0], IR[1], not_1_out[2], not_1_out[3], not_1_out[4], IR[5], not_1_out[6], not_1_out[7]);
  nand nand_30 (LDYI, IR[0], IR[1], not_1_out[2], not_1_out[3], not_1_out[4], IR[5], not_1_out[6], not_1_out[7]);
  nand nand_31 (LDA, not_1_out[0], not_1_out[1], IR[2], not_1_out[3], not_1_out[4], IR[5], not_1_out[6], not_1_out[7]);
  nand nand_32 (LDAI, IR[0], not_1_out[1], IR[2], not_1_out[3], not_1_out[4], IR[5], not_1_out[6], not_1_out[7]);
  nand nand_33 (MXY, not_1_out[0], IR[1], IR[2], not_1_out[3], not_1_out[4], IR[5], not_1_out[6], not_1_out[7]);
  nand nand_34 (MXA, IR[0], IR[1], IR[2], not_1_out[3], not_1_out[4], IR[5], not_1_out[6], not_1_out[7]);
  nand nand_35 (MYX, not_1_out[0], not_1_out[1], not_1_out[2], IR[3], not_1_out[4], IR[5], not_1_out[6], not_1_out[7]);
  nand nand_36 (MYA, IR[0], not_1_out[1], not_1_out[2], IR[3], not_1_out[4], IR[5], not_1_out[6], not_1_out[7]);
  nand nand_37 (MAX, not_1_out[0], IR[1], not_1_out[2], IR[3], not_1_out[4], IR[5], not_1_out[6], not_1_out[7]);
  nand nand_38 (MAY, IR[0], IR[1], not_1_out[2], IR[3], not_1_out[4], IR[5], not_1_out[6], not_1_out[7]);
  nand nand_39 (ANX, not_1_out[0], not_1_out[1], not_1_out[2], not_1_out[3], IR[4], IR[5], not_1_out[6], not_1_out[7]);
  nand nand_40 (ANY, IR[0], not_1_out[1], not_1_out[2], not_1_out[3], IR[4], IR[5], not_1_out[6], not_1_out[7]);
  nand nand_41 (ANA, not_1_out[0], IR[1], not_1_out[2], not_1_out[3], IR[4], IR[5], not_1_out[6], not_1_out[7]);
  nand nand_42 (ANI, IR[0], IR[1], not_1_out[2], not_1_out[3], IR[4], IR[5], not_1_out[6], not_1_out[7]);
  nand nand_43 (ORX, not_1_out[0], not_1_out[1], IR[2], not_1_out[3], IR[4], IR[5], not_1_out[6], not_1_out[7]);
  nand nand_44 (ORY, not_1_out[0], not_1_out[1], IR[2], not_1_out[3], IR[4], IR[5], not_1_out[6], not_1_out[7]);
  nand nand_45 (ORA, IR[0], not_1_out[1], IR[2], not_1_out[3], IR[4], IR[5], not_1_out[6], not_1_out[7]);
  nand nand_46 (ORI, not_1_out[0], IR[1], IR[2], not_1_out[3], IR[4], IR[5], not_1_out[6], not_1_out[7]);
  nand nand_47 (XOX, IR[0], IR[1], IR[2], not_1_out[3], IR[4], IR[5], not_1_out[6], not_1_out[7]);
  nand nand_48 (XOY, not_1_out[0], not_1_out[1], not_1_out[2], IR[3], IR[4], IR[5], not_1_out[6], not_1_out[7]);
  nand nand_49 (XOA, IR[0], not_1_out[1], not_1_out[2], IR[3], IR[4], IR[5], not_1_out[6], not_1_out[7]);
  nand nand_50 (XOI, not_1_out[0], IR[1], not_1_out[2], IR[3], IR[4], IR[5], not_1_out[6], not_1_out[7]);
  nand nand_51 (NOX, IR[0], IR[1], not_1_out[2], IR[3], IR[4], IR[5], not_1_out[6], not_1_out[7]);
  nand nand_52 (NOY, not_1_out[0], not_1_out[1], IR[2], IR[3], IR[4], IR[5], not_1_out[6], not_1_out[7]);
  nand nand_53 (NOA, IR[0], not_1_out[1], IR[2], IR[3], IR[4], IR[5], not_1_out[6], not_1_out[7]);
  nand nand_54 (NOI, not_1_out[0], IR[1], IR[2], IR[3], IR[4], IR[5], not_1_out[6], not_1_out[7]);
  nand nand_55 (STX, not_1_out[0], not_1_out[1], not_1_out[2], not_1_out[3], not_1_out[4], not_1_out[5], IR[6], not_1_out[7]);
  nand nand_56 (STY, IR[0], not_1_out[1], not_1_out[2], not_1_out[3], not_1_out[4], not_1_out[5], IR[6], not_1_out[7]);
  nand nand_57 (STA, not_1_out[0], IR[1], not_1_out[2], not_1_out[3], not_1_out[4], not_1_out[5], IR[6], not_1_out[7]);
  nand nand_58 (LSX, IR[0], IR[1], not_1_out[2], not_1_out[3], not_1_out[4], not_1_out[5], IR[6], not_1_out[7]);
  nand nand_59 (LSY, not_1_out[0], not_1_out[1], IR[2], not_1_out[3], not_1_out[4], not_1_out[5], IR[6], not_1_out[7]);
  nand nand_60 (LSA, IR[0], not_1_out[1], IR[2], not_1_out[3], not_1_out[4], not_1_out[5], IR[6], not_1_out[7]);
endmodule

module Tring (
  input  CLK,
  input  CLR,
  output [15:0] T
);

  wire j_k_ff_1_q, j_k_ff_2_qn, j_k_ff_3_qn, j_k_ff_4_qn, j_k_ff_5_qn, j_k_ff_6_qn, j_k_ff_7_qn, j_k_ff_8_qn,
       j_k_ff_9_qn, j_k_ff_10_qn, j_k_ff_11_qn, j_k_ff_12_qn, j_k_ff_13_qn, j_k_ff_14_qn, j_k_ff_15_qn,
       j_k_ff_16_qn;

  J_K_Flip_Flop j_k_ff_1 (
    .J(j_k_ff_16_qn), .K(T[15]), .clk(CLK), .Q(j_k_ff_1_q), .Qn(T[0]), .preset(1'b0), .reset(CLR));
  J_K_Flip_Flop j_k_ff_2 (.J(T[0]), .K(j_k_ff_1_q), .clk(CLK), .Q(T[1]), .Qn(j_k_ff_2_qn), .preset(1'b0), .reset(CLR));
  J_K_Flip_Flop j_k_ff_3 (.J(T[1]), .K(j_k_ff_2_qn), .clk(CLK), .Q(T[2]), .Qn(j_k_ff_3_qn), .preset(1'b0), .reset(CLR));
  J_K_Flip_Flop j_k_ff_4 (.J(T[2]), .K(j_k_ff_3_qn), .clk(CLK), .Q(T[3]), .Qn(j_k_ff_4_qn), .preset(1'b0), .reset(CLR));
  J_K_Flip_Flop j_k_ff_5 (.J(T[3]), .K(j_k_ff_4_qn), .clk(CLK), .Q(T[4]), .Qn(j_k_ff_5_qn), .preset(1'b0), .reset(CLR));
  J_K_Flip_Flop j_k_ff_6 (.J(T[4]), .K(j_k_ff_5_qn), .clk(CLK), .Q(T[5]), .Qn(j_k_ff_6_qn), .preset(1'b0), .reset(CLR));
  J_K_Flip_Flop j_k_ff_7 (.J(T[5]), .K(j_k_ff_6_qn), .clk(CLK), .Q(T[6]), .Qn(j_k_ff_7_qn), .preset(1'b0), .reset(CLR));
  J_K_Flip_Flop j_k_ff_8 (.J(T[6]), .K(j_k_ff_7_qn), .clk(CLK), .Q(T[7]), .Qn(j_k_ff_8_qn), .preset(1'b0), .reset(CLR));
  J_K_Flip_Flop j_k_ff_9 (.J(T[7]), .K(j_k_ff_8_qn), .clk(CLK), .Q(T[8]), .Qn(j_k_ff_9_qn), .preset(1'b0), .reset(CLR));
  J_K_Flip_Flop j_k_ff_10 (
    .J(T[8]), .K(j_k_ff_9_qn), .clk(CLK), .Q(T[9]), .Qn(j_k_ff_10_qn), .preset(1'b0), .reset(CLR));
  J_K_Flip_Flop j_k_ff_11 (
    .J(T[9]), .K(j_k_ff_10_qn), .clk(CLK), .Q(T[10]), .Qn(j_k_ff_11_qn), .preset(1'b0), .reset(CLR));
  J_K_Flip_Flop j_k_ff_12 (
    .J(T[10]), .K(j_k_ff_11_qn), .clk(CLK), .Q(T[11]), .Qn(j_k_ff_12_qn), .preset(1'b0), .reset(CLR));
  J_K_Flip_Flop j_k_ff_13 (
    .J(T[11]), .K(j_k_ff_12_qn), .clk(CLK), .Q(T[12]), .Qn(j_k_ff_13_qn), .preset(1'b0), .reset(CLR));
  J_K_Flip_Flop j_k_ff_14 (
    .J(T[12]), .K(j_k_ff_13_qn), .clk(CLK), .Q(T[13]), .Qn(j_k_ff_14_qn), .preset(1'b0), .reset(CLR));
  J_K_Flip_Flop j_k_ff_15 (
    .J(T[13]), .K(j_k_ff_14_qn), .clk(CLK), .Q(T[14]), .Qn(j_k_ff_15_qn), .preset(1'b0), .reset(CLR));
  J_K_Flip_Flop j_k_ff_16 (
    .J(T[14]), .K(j_k_ff_15_qn), .clk(CLK), .Q(T[15]), .Qn(j_k_ff_16_qn), .preset(1'b0), .reset(CLR));
endmodule

module dec2 (
  input  [7:0] IR,
  output NOP,
  output CLX,
  output CLY,
  output CLA,
  output OUX,
  output OUY,
  output OUA,
  output CMX,
  output CMY,
  output CMA,
  output CMI,
  output CALL,
  output RET,
  output HLT,
  output JZ,
  output JNZ,
  output JN,
  output JL,
  output JG,
  output JE,
  output ADX,
  output ADY,
  output ADA,
  output ADI,
  output SUX,
  output SUY,
  output SUA,
  output SUI,
  output LDX,
  output LDXI,
  output LDY,
  output LDYI,
  output LDA,
  output LDAI,
  output MXY,
  output MXA,
  output MYX,
  output MYA,
  output MAX,
  output MAY,
  output STX,
  output STY,
  output STA,
  output ANX,
  output ANY,
  output ANA,
  output ANI,
  output ORX,
  output ORY,
  output ORA,
  output ORI,
  output XOX,
  output XOY,
  output XOA,
  output XOI,
  output NOX,
  output NOY,
  output NOA,
  output NOI
);

  wire decoder_1_out0, decoder_1_out1, decoder_1_out2, decoder_1_out3, decoder_1_out4, decoder_1_out5,
       decoder_1_out6, decoder_1_out7;

  Decoder #(.select(3)) decoder_1 (
    .out0(decoder_1_out0), .out1(decoder_1_out1), .out2(decoder_1_out2), .out3(decoder_1_out3),
    .out4(decoder_1_out4), .out5(decoder_1_out5), .out6(decoder_1_out6), .out7(decoder_1_out7),
    .sel(IR[6:4]), .en(1'b1));
  Decoder #(.select(3)) decoder_2 (
    .out0(NOP), .out1(CLX), .out2(CLY), .out3(CLA), .out4(OUX), .out5(OUY), .out6(OUA), .out7(CMX),
    .sel(IR[2:0]), .en(decoder_1_out0));
  Decoder #(.select(3)) decoder_3 (
    .out0(CMY), .out1(CMA), .out2(CMI), .out3(CALL), .out4(RET), .out5(HLT), .sel(IR[2:0]),
    .en(decoder_1_out1));  // open: out6, out7
  Decoder #(.select(3)) decoder_4 (
    .out0(JZ), .out1(JNZ), .out2(JN), .out3(JL), .out4(JG), .out5(JE), .sel(IR[2:0]), .en(decoder_1_out2));  // open: out6, out7
  Decoder #(.select(3)) decoder_5 (
    .out0(ADX), .out1(ADY), .out2(ADA), .out3(ADI), .out4(SUX), .out5(SUY), .out6(SUA), .out7(SUI),
    .sel(IR[2:0]), .en(decoder_1_out3));
  Decoder #(.select(3)) decoder_6 (
    .out0(LDX), .out1(LDXI), .out2(LDY), .out3(LDYI), .out4(LDA), .out5(LDAI), .out6(MXY), .out7(MXA),
    .sel(IR[2:0]), .en(decoder_1_out4));
  Decoder #(.select(3)) decoder_7 (
    .out0(MYX), .out1(MYA), .out2(MAX), .out3(MAY), .out4(STX), .out5(STY), .out6(STA), .sel(IR[2:0]),
    .en(decoder_1_out5));  // open: out7
  Decoder #(.select(3)) decoder_8 (
    .out0(ANX), .out1(ANY), .out2(ANA), .out3(ANI), .out4(ORX), .out5(ORY), .out6(ORA), .out7(ORI),
    .sel(IR[2:0]), .en(decoder_1_out6));
  Decoder #(.select(3)) decoder_9 (
    .out0(XOX), .out1(XOY), .out2(XOA), .out3(XOI), .out4(NOX), .out5(NOY), .out6(NOA), .out7(NOI),
    .sel(IR[2:0]), .en(decoder_1_out7));
endmodule
