// Logisim project Control.circ as structural Verilog: 2 circuits, main circuit main
module main (
  output INC,
  output ENpcLDm,
  output ENramLDir,
  output ENir
);

  wire buffer_1_out, clock_1_out, dipswitch_1_p1, dipswitch_1_p2, dipswitch_1_p3, dipswitch_1_p4,
       dipswitch_1_p5, dipswitch_1_p6, dipswitch_1_p7, dipswitch_1_p8, not_1_out, not_3_out, not_4_out,
       not_5_out, not_6_out, not_7_out, not_8_out, not_9_out, not_10_out, or_1_out, or_2_out, or_3_out,
       TRing_t3, TRing_t9;

  Clock clock_1 (.out(clock_1_out));
  buf buffer_1 (buffer_1_out, INC);
  not not_1 (not_1_out, or_1_out);
  or or_1 (or_1_out, TRing_t3, ENir);
  not not_2 (ENir, or_2_out);
  or or_2 (or_2_out, not_1_out, or_3_out);
  ring TRing (
    .CLK(clock_1_out), .T0(INC), .T1(ENpcLDm), .T2(ENramLDir), .T3(TRing_t3), .T9(TRing_t9));  // open: CLR, T4, T5, T6, T7, T8
  or or_3 (or_3_out, TRing_t9, buffer_1_out);
  not not_3 (not_3_out, dipswitch_1_p1);
  not not_4 (not_4_out, dipswitch_1_p2);
  not not_5 (not_5_out, dipswitch_1_p3);
  not not_6 (not_6_out, dipswitch_1_p4);
  not not_7 (not_7_out, dipswitch_1_p5);
  not not_8 (not_8_out, dipswitch_1_p6);
  not not_9 (not_9_out, dipswitch_1_p7);
  not not_10 (not_10_out, dipswitch_1_p8);
  // DipSwitch dipswitch_1: pin names not known; wires that end beside it: dipswitch_1_p1, dipswitch_1_p2, dipswitch_1_p3, dipswitch_1_p4, dipswitch_1_p5, dipswitch_1_p6, dipswitch_1_p7, dipswitch_1_p8
  // AND_Gate HTL has open pins: in0=dipswitch_1_p8, in1=not_9_out, in2=not_8_out, in3=not_7_out, in4=not_6_out, in5=not_5_out, in6=not_4_out, in7=not_3_out, out=open
  // AND_Gate MXA has open pins: in0=not_10_out, in1=dipswitch_1_p7, in2=not_8_out, in3=not_7_out, in4=not_6_out, in5=not_5_out, in6=not_4_out, in7=not_3_out, out=open
  // AND_Gate MXY has open pins: in0=dipswitch_1_p8, in1=dipswitch_1_p7, in2=not_8_out, in3=not_7_out, in4=not_6_out, in5=not_5_out, in6=not_4_out, in7=not_3_out, out=open
  // AND_Gate MYA has open pins: in0=not_10_out, in1=not_9_out, in2=dipswitch_1_p6, in3=not_7_out, in4=not_6_out, in5=not_5_out, in6=not_4_out, in7=not_3_out, out=open
  // AND_Gate MYX has open pins: in0=dipswitch_1_p8, in1=not_9_out, in2=dipswitch_1_p6, in3=not_7_out, in4=not_6_out, in5=not_5_out, in6=not_4_out, in7=not_3_out, out=open
  // AND_Gate MAX has open pins: in0=not_10_out, in1=dipswitch_1_p7, in2=dipswitch_1_p6, in3=not_7_out, in4=not_6_out, in5=not_5_out, in6=not_4_out, in7=not_3_out, out=open
  // AND_Gate MAY has open pins: in0=dipswitch_1_p8, in1=dipswitch_1_p7, in2=dipswitch_1_p6, in3=not_7_out, in4=not_6_out, in5=not_5_out, in6=not_4_out, in7=not_3_out, out=open
  // AND_Gate STA has open pins: in0=not_10_out, in1=not_9_out, in2=not_8_out, in3=dipswitch_1_p5, in4=not_6_out, in5=not_5_out, in6=not_4_out, in7=not_3_out, out=open
  // AND_Gate CLL has open pins: in0=dipswitch_1_p8, in1=not_9_out, in2=not_8_out, in3=dipswitch_1_p5, in4=not_6_out, in5=not_5_out, in6=not_4_out, in7=not_3_out, out=open
  // AND_Gate RET has open pins: in0=not_10_out, in1=dipswitch_1_p7, in2=not_8_out, in3=dipswitch_1_p5, in4=not_6_out, in5=not_5_out, in6=not_4_out, in7=not_3_out, out=open
  // AND_Gate INP has open pins: in0=dipswitch_1_p8, in1=dipswitch_1_p7, in2=not_8_out, in3=dipswitch_1_p5, in4=not_6_out, in5=not_5_out, in6=not_4_out, in7=not_3_out, out=open
  // AND_Gate LDP has open pins: in0=not_10_out, in1=not_9_out, in2=dipswitch_1_p6, in3=dipswitch_1_p5, in4=not_6_out, in5=not_5_out, in6=not_4_out, in7=not_3_out, out=open
  // AND_Gate LDA has open pins: in0=dipswitch_1_p8, in1=not_9_out, in2=dipswitch_1_p6, in3=dipswitch_1_p5, in4=not_6_out, in5=not_5_out, in6=not_4_out, in7=not_3_out, out=open
  // AND_Gate LDT has open pins: in0=not_10_out, in1=dipswitch_1_p7, in2=dipswitch_1_p6, in3=dipswitch_1_p5, in4=not_6_out, in5=not_5_out, in6=not_4_out, in7=not_3_out, out=open
  // AND_Gate LDX has open pins: in0=dipswitch_1_p8, in1=dipswitch_1_p7, in2=dipswitch_1_p6, in3=dipswitch_1_p5, in4=not_6_out, in5=not_5_out, in6=not_4_out, in7=not_3_out, out=open
  // AND_Gate LDY has open pins: in0=not_10_out, in1=not_9_out, in2=not_8_out, in3=not_7_out, in4=dipswitch_1_p4, in5=not_5_out, in6=not_4_out, in7=not_3_out, out=open
  // AND_Gate INA has open pins: in0=dipswitch_1_p8, in1=not_9_out, in2=not_8_out, in3=not_7_out, in4=dipswitch_1_p4, in5=not_5_out, in6=not_4_out, in7=not_3_out, out=open
  // AND_Gate ADX has open pins: in0=not_10_out, in1=dipswitch_1_p7, in2=not_8_out, in3=not_7_out, in4=dipswitch_1_p4, in5=not_5_out, in6=not_4_out, in7=not_3_out, out=open
  // AND_Gate ADY has open pins: in0=dipswitch_1_p8, in1=dipswitch_1_p7, in2=not_8_out, in3=not_7_out, in4=dipswitch_1_p4, in5=not_5_out, in6=not_4_out, in7=not_3_out, out=open
  // AND_Gate SUX has open pins: in0=not_10_out, in1=not_9_out, in2=dipswitch_1_p6, in3=not_7_out, in4=dipswitch_1_p4, in5=not_5_out, in6=not_4_out, in7=not_3_out, out=open
  // AND_Gate SUY has open pins: in0=dipswitch_1_p8, in1=not_9_out, in2=dipswitch_1_p6, in3=not_7_out, in4=dipswitch_1_p4, in5=not_5_out, in6=not_4_out, in7=not_3_out, out=open
  // AND_Gate CMA has open pins: in0=not_10_out, in1=dipswitch_1_p7, in2=dipswitch_1_p6, in3=not_7_out, in4=dipswitch_1_p4, in5=not_5_out, in6=not_4_out, in7=not_3_out, out=open
  // AND_Gate CMP has open pins: in0=dipswitch_1_p8, in1=dipswitch_1_p7, in2=dipswitch_1_p6, in3=not_7_out, in4=dipswitch_1_p4, in5=not_5_out, in6=not_4_out, in7=not_3_out, out=open
  // AND_Gate JMP has open pins: in0=not_10_out, in1=not_9_out, in2=not_8_out, in3=dipswitch_1_p5, in4=dipswitch_1_p4, in5=not_5_out, in6=not_4_out, in7=not_3_out, out=open
  // AND_Gate JZR has open pins: in0=dipswitch_1_p8, in1=not_9_out, in2=not_8_out, in3=dipswitch_1_p5, in4=dipswitch_1_p4, in5=not_5_out, in6=not_4_out, in7=not_3_out, out=open
  // AND_Gate JNZ has open pins: in0=not_10_out, in1=dipswitch_1_p7, in2=not_8_out, in3=dipswitch_1_p5, in4=dipswitch_1_p4, in5=not_5_out, in6=not_4_out, in7=not_3_out, out=open
  // AND_Gate JLD has open pins: in0=dipswitch_1_p8, in1=dipswitch_1_p7, in2=not_8_out, in3=dipswitch_1_p5, in4=dipswitch_1_p4, in5=not_5_out, in6=not_4_out, in7=not_3_out, out=open
  // AND_Gate JGD has open pins: in0=not_10_out, in1=not_9_out, in2=dipswitch_1_p6, in3=dipswitch_1_p5, in4=dipswitch_1_p4, in5=not_5_out, in6=not_4_out, in7=not_3_out, out=open
  // AND_Gate JEQ has open pins: in0=dipswitch_1_p8, in1=not_9_out, in2=dipswitch_1_p6, in3=dipswitch_1_p5, in4=dipswitch_1_p4, in5=not_5_out, in6=not_4_out, in7=not_3_out, out=open
  // AND_Gate LDO has open pins: in0=not_10_out, in1=dipswitch_1_p7, in2=dipswitch_1_p6, in3=dipswitch_1_p5, in4=dipswitch_1_p4, in5=not_5_out, in6=not_4_out, in7=not_3_out, out=open
endmodule

module ring (
  input  CLK,
  input  CLR,
  output T0,
  output T1,
  output T2,
  output T5,
  output T3,
  output T4,
  output T6,
  output T7,
  output T8,
  output T9
);

  wire j_k_ff_1_q, j_k_ff_2_qn, j_k_ff_3_qn, j_k_ff_4_qn, j_k_ff_5_qn, j_k_ff_6_qn, j_k_ff_7_qn, j_k_ff_8_qn,
       j_k_ff_9_qn, j_k_ff_10_qn;

  J_K_Flip_Flop j_k_ff_1 (.J(j_k_ff_10_qn), .K(T9), .clk(CLK), .Q(j_k_ff_1_q), .Qn(T0), .preset(1'b0), .reset(CLR));
  J_K_Flip_Flop j_k_ff_2 (.J(T0), .K(j_k_ff_1_q), .clk(CLK), .Q(T1), .Qn(j_k_ff_2_qn), .preset(1'b0), .reset(CLR));
  J_K_Flip_Flop j_k_ff_3 (.J(T1), .K(j_k_ff_2_qn), .clk(CLK), .Q(T2), .Qn(j_k_ff_3_qn), .preset(1'b0), .reset(CLR));
  J_K_Flip_Flop j_k_ff_4 (.J(T2), .K(j_k_ff_3_qn), .clk(CLK), .Q(T3), .Qn(j_k_ff_4_qn), .preset(1'b0), .reset(CLR));
  J_K_Flip_Flop j_k_ff_5 (.J(T3), .K(j_k_ff_4_qn), .clk(CLK), .Q(T4), .Qn(j_k_ff_5_qn), .preset(1'b0), .reset(CLR));
  J_K_Flip_Flop j_k_ff_6 (.J(T4), .K(j_k_ff_5_qn), .clk(CLK), .Q(T5), .Qn(j_k_ff_6_qn), .preset(1'b0), .reset(CLR));
  J_K_Flip_Flop j_k_ff_7 (.J(T5), .K(j_k_ff_6_qn), .clk(CLK), .Q(T6), .Qn(j_k_ff_7_qn), .preset(1'b0), .reset(CLR));
  J_K_Flip_Flop j_k_ff_8 (.J(T6), .K(j_k_ff_7_qn), .clk(CLK), .Q(T7), .Qn(j_k_ff_8_qn), .preset(1'b0), .reset(CLR));
  J_K_Flip_Flop j_k_ff_9 (.J(T7), .K(j_k_ff_8_qn), .clk(CLK), .Q(T8), .Qn(j_k_ff_9_qn), .preset(1'b0), .reset(CLR));
  J_K_Flip_Flop j_k_ff_10 (.J(T8), .K(j_k_ff_9_qn), .clk(CLK), .Q(T9), .Qn(j_k_ff_10_qn), .preset(1'b0), .reset(CLR));
endmodule
