// Logisim project sim.circ as structural Verilog
module main (
);

  wire clock_1_out;
  wire [7:0] register_1_q;

  Clock clock_1 (.out(clock_1_out));
  Register register_1 (.D(register_1_q), .clk(clock_1_out), .Q(register_1_q), .clr(1'b0));  // open: en
  Register register_2 (.D(register_1_q), .clk(clock_1_out), .Q(register_1_q), .clr(1'b0));  // open: en
  ALU alu_1 (.CLK(clock_1_out), .W(register_1_q));  // open: LDA, ADD, SUB, LDT, ZERO, NEGATIVE, OVERFLOW
  PC pc_1 (.W(register_1_q));  // open: PCL, PCH, CLK, LDP, LDP2, LDP1, INP, CLR
endmodule

module PC (
  input  CLR,
  input  CLK,
  input  INP,
  input  [7:0] W,
  input  LDP1,
  input  LDP,
  input  LDP2,
  output [7:0] PCL,
  output [7:0] PCH
);

  wire and_1_out, or_1_out;
  wire [7:0] register_1_q, register_2_q;

  and and_1 (and_1_out, LDP, CLK);
  Register register_1 (.D(W), .en(LDP1), .clk(CLK), .Q(register_1_q), .clr(CLR));
  or or_1 (or_1_out, and_1_out, PCL[7]);
  Register register_2 (.D(W), .en(LDP2), .clk(CLK), .Q(register_2_q), .clr(CLR));
  Counter #(.trigger("falling")) counter_1 (
    .clr(CLR), .load(LDP), .up(1'b1), .count(1'b1), .clk(INP), .D(register_1_q), .Q(PCL));  // open: carry
  Counter #(.trigger("falling")) counter_2 (
    .clr(CLR), .load(LDP), .up(1'b1), .count(1'b1), .clk(or_1_out), .D(register_2_q), .Q(PCH));  // open: carry
endmodule

module RING (
  input  CLK,
  input  CLR,
  output [17:0] T
);

  wire j_k_ff_1_q, j_k_ff_2_qn, j_k_ff_3_qn, j_k_ff_4_qn, j_k_ff_5_qn, j_k_ff_6_qn, j_k_ff_7_qn, j_k_ff_8_qn,
       j_k_ff_9_qn, j_k_ff_10_qn, j_k_ff_11_qn, j_k_ff_12_qn, j_k_ff_13_qn, j_k_ff_14_qn, j_k_ff_15_qn,
       j_k_ff_16_qn, j_k_ff_17_qn, j_k_ff_18_qn;

  J_K_Flip_Flop j_k_ff_1 (
    .J(j_k_ff_18_qn), .K(T[17]), .clk(CLK), .Q(j_k_ff_1_q), .Qn(T[0]), .preset(1'b0), .reset(CLR));
  J_K_Flip_Flop j_k_ff_2 (.J(T[0]), .K(j_k_ff_1_q), .clk(CLK), .Q(T[1]), .Qn(j_k_ff_2_qn), .preset(1'b0), .reset(CLR));
  J_K_Flip_Flop j_k_ff_3 (.J(T[1]), .K(j_k_ff_2_qn), .clk(CLK), .Q(T[2]), .Qn(j_k_ff_3_qn), .preset(1'b0), .reset(CLR));
  J_K_Flip_Flop j_k_ff_4 (.J(T[2]), .K(j_k_ff_3_qn), .clk(CLK), .Q(T[3]), .Qn(j_k_ff_4_qn), .preset(1'b0), .reset(CLR));
  J_K_Flip_Flop j_k_ff_5 (.J(T[3]), .K(j_k_ff_4_qn), .clk(CLK), .Q(T[4]), .Qn(j_k_ff_5_qn), .preset(1'b0), .reset(CLR));
  J_K_Flip_Flop j_k_ff_6 (.J(T[4]), .K(j_k_ff_5_qn), .clk(CLK), .Q(T[5]), .Qn(j_k_ff_6_qn), .preset(1'b0), .reset(CLR));
  J_K_Flip_Flop j_k_ff_7 (.J(T[5]), .K(j_k_ff_6_qn), .clk(CLK), .Q(T[6]), .Qn(j_k_ff_7_qn), .preset(1'b0), .reset(CLR));
  J_K_Flip_Flop j_k_ff_8 (.J(T[6]), .K(j_k_ff_7_qn), .clk(CLK), .Q(T[7]), .Qn(j_k_ff_8_qn), .preset(1'b0), .reset(CLR));
  J_K_Flip_Flop j_k_ff_9 (.J(T[7]), .K(j_k_ff_8_qn), .clk(CLK), .Q(T[8]), .Qn(j_k_ff_9_qn), .preset(1'b0), .reset(CLR));
  J_K_Flip_Flop j_k_ff_10 (
    .J(T[8]), .K(j_k_ff_9_qn), .clk(CLK), .Q(T[9]), .Qn(j_k_ff_10_qn), .preset(1'b0), .reset(CLR));
  J_K_Flip_Flop j_k_ff_11 (
    .J(T[9]), .K(j_k_ff_10_qn), .clk(CLK), .Q(T[10]), .Qn(j_k_ff_11_qn), .preset(1'b0), .reset(CLR));
  J_K_Flip_Flop j_k_ff_12 (
    .J(T[10]), .K(j_k_ff_11_qn), .clk(CLK), .Q(T[11]), .Qn(j_k_ff_12_qn), .preset(1'b0), .reset(CLR));
  J_K_Flip_Flop j_k_ff_13 (
    .J(T[11]), .K(j_k_ff_12_qn), .clk(CLK), .Q(T[12]), .Qn(j_k_ff_13_qn), .preset(1'b0), .reset(CLR));
  J_K_Flip_Flop j_k_ff_14 (
    .J(T[12]), .K(j_k_ff_13_qn), .clk(CLK), .Q(T[13]), .Qn(j_k_ff_14_qn), .preset(1'b0), .reset(CLR));
  J_K_Flip_Flop j_k_ff_15 (
    .J(T[13]), .K(j_k_ff_14_qn), .clk(CLK), .Q(T[14]), .Qn(j_k_ff_15_qn), .preset(1'b0), .reset(CLR));
  J_K_Flip_Flop j_k_ff_16 (
    .J(T[14]), .K(j_k_ff_15_qn), .clk(CLK), .Q(T[15]), .Qn(j_k_ff_16_qn), .preset(1'b0), .reset(CLR));
  J_K_Flip_Flop j_k_ff_17 (
    .J(T[15]), .K(j_k_ff_16_qn), .clk(CLK), .Q(T[16]), .Qn(j_k_ff_17_qn), .preset(1'b0), .reset(CLR));
  J_K_Flip_Flop j_k_ff_18 (
    .J(T[16]), .K(j_k_ff_17_qn), .clk(CLK), .Q(T[17]), .Qn(j_k_ff_18_qn), .preset(1'b0), .reset(CLR));
endmodule

module ALU (
  input  CLK,
  input  [7:0] W,
  input  LDA,
  input  ADD,
  input  SUB,
  input  LDT,
  output ZERO,
  output NEGATIVE,
  output OVERFLOW
);

  wire or_1_out;
  wire [7:0] addsub_1_outacc, or_2_out, register_1_q, register_2_q;

  or or_1 (or_1_out, LDA, SUB, ADD);
  assign or_2_out = addsub_1_outacc | W;  // OR_Gate or_2, 8 bits wide
  Register register_1 (.D(or_2_out), .en(or_1_out), .clk(CLK), .Q(register_1_q), .clr(1'b0));
  Register register_2 (.D(W), .en(LDT), .clk(CLK), .Q(register_2_q), .clr(1'b0));
  ADDSUB addsub_1 (
    .ACC(register_1_q), .SUB(SUB), .TMP(register_2_q), .OUTACC(addsub_1_outacc), .ZERO(ZERO),
    .NEGATIVE(NEGATIVE), .OVERFLOW(OVERFLOW));
endmodule

module ADDSUB (
  input  [7:0] ACC,
  input  SUB,
  input  [7:0] TMP,
  output [7:0] OUTACC,
  output ZERO,
  output NEGATIVE,
  output OVERFLOW
);

  wire fulladder_1_co, fulladder_2_co, fulladder_3_co, fulladder_4_co, fulladder_5_co, fulladder_6_co,
       fulladder_7_co, not_1_out, or_1_out, xor_1_out, xor_2_out, xor_3_out, xor_4_out, xor_5_out, xor_6_out,
       xor_7_out, xor_8_out;

  xor xor_1 (xor_1_out, SUB, TMP[0]);
  xor xor_2 (xor_2_out, SUB, TMP[1]);
  xor xor_3 (xor_3_out, SUB, TMP[2]);
  xor xor_4 (xor_4_out, SUB, TMP[3]);
  xor xor_5 (xor_5_out, SUB, TMP[4]);
  xor xor_6 (xor_6_out, SUB, TMP[5]);
  xor xor_7 (xor_7_out, SUB, TMP[6]);
  xor xor_8 (xor_8_out, SUB, TMP[7]);
  or or_1 (or_1_out, SUB, ACC[0]);
  FULLADDER fulladder_1 (.CI(1'b0), .A(or_1_out), .B(xor_1_out), .S(OUTACC[0]), .CO(fulladder_1_co));
  FULLADDER fulladder_2 (.CI(fulladder_1_co), .A(ACC[1]), .B(xor_2_out), .S(OUTACC[1]), .CO(fulladder_2_co));
  FULLADDER fulladder_3 (.CI(fulladder_2_co), .A(ACC[2]), .B(xor_3_out), .S(OUTACC[2]), .CO(fulladder_3_co));
  FULLADDER fulladder_4 (.CI(fulladder_3_co), .A(ACC[3]), .B(xor_4_out), .S(OUTACC[3]), .CO(fulladder_4_co));
  FULLADDER fulladder_5 (.CI(fulladder_4_co), .A(ACC[4]), .B(xor_5_out), .S(OUTACC[4]), .CO(fulladder_5_co));
  FULLADDER fulladder_6 (.CI(fulladder_5_co), .A(ACC[5]), .B(xor_6_out), .S(OUTACC[5]), .CO(fulladder_6_co));
  FULLADDER fulladder_7 (.CI(fulladder_6_co), .A(ACC[6]), .B(xor_7_out), .S(OUTACC[6]), .CO(fulladder_7_co));
  FULLADDER fulladder_8 (.CI(fulladder_7_co), .A(ACC[7]), .B(xor_8_out), .S(NEGATIVE), .CO(OVERFLOW));
  not not_1 (not_1_out, NEGATIVE);
  and and_1 (ZERO, OUTACC[0], OUTACC[1], OUTACC[2], OUTACC[3], OUTACC[4], OUTACC[5], OUTACC[6], not_1_out);

  assign OUTACC[7] = NEGATIVE;
endmodule

module FULLADDER (
  input  CI,
  input  A,
  input  B,
  output S,
  output CO
);

  wire and_1_out, and_2_out, xor_1_out;

  xor xor_1 (xor_1_out, A, B);
  and and_1 (and_1_out, A, B);
  xor xor_2 (S, CI, xor_1_out);
  and and_2 (and_2_out, CI, xor_1_out);
  or or_1 (CO, and_2_out, and_1_out);
endmodule

module DECODERROM (
  input  [7:0] IR,
  output HLT,
  output MAT,
  output MAX,
  output MAY,
  output MXA,
  output MXY
);

  wire [7:0] not_1_out;

  assign not_1_out = ~IR;  // NOT_Gate not_1, 8 bits wide
  and and_1 (HLT, IR[0], not_1_out[1], not_1_out[2], not_1_out[3], not_1_out[4], not_1_out[5], not_1_out[6], not_1_out[7]);
  and and_2 (MAT, not_1_out[0], IR[1], not_1_out[2], not_1_out[3], not_1_out[4], not_1_out[5], not_1_out[6], not_1_out[7]);
  and and_3 (MAX, IR[0], IR[1], not_1_out[2], not_1_out[3], not_1_out[4], not_1_out[5], not_1_out[6], not_1_out[7]);
  and and_4 (MAY, not_1_out[0], not_1_out[1], IR[2], not_1_out[3], not_1_out[4], not_1_out[5], not_1_out[6], not_1_out[7]);
  and and_5 (MXA, IR[0], not_1_out[1], IR[2], not_1_out[3], not_1_out[4], not_1_out[5], not_1_out[6], not_1_out[7]);
  and and_6 (MXY, not_1_out[0], IR[1], IR[2], not_1_out[3], not_1_out[4], not_1_out[5], not_1_out[6], not_1_out[7]);
endmodule
